// Logisim project trafficlight.circ as structural Verilog: 3 circuits, main circuit main
module main (
);

  wire and_2_out, and_3_out, and_4_out, clock_1_out, d_ff_1_q, d_ff_1_qn, delay_1_four, delay_1_twenty_five,
       delay_1_two, lights_1_s0, lights_1_s1, lights_1_s2, lights_1_y1, lights_1_y2, lights_1_y3,
       lights_1_y4, lights_1_y5, lights_1_y6, multiplexer_1_out, multiplexer_2_out, not_1_out, not_2_out,
       not_3_out, not_4_out, or_1_out, or_2_out, or_3_out, shift_register_1_p1, undriven;
  wire [4:0] delay_1_delay;

  Clock clock_1 (.out(clock_1_out));
  not not_1 (not_1_out, d_ff_1_q);
  // Shift_Register #(.parallel("false")) shift_register_1: pin names not known; wires that end beside it: shift_register_1_p1, 1'b0
  or or_1 (or_1_out, not_1_out, and_2_out);
  and and_1 (shift_register_1_p1, or_1_out, clock_1_out);
  delay delay_1 (
    .clk(clock_1_out), .Twenty_five(delay_1_twenty_five), .Four(delay_1_four), .Two(delay_1_two),
    .S2(lights_1_s2), .S1(lights_1_s1), .S0(lights_1_s0), .Delay(delay_1_delay));
  not not_2 (not_2_out, lights_1_s2);
  and and_2 (and_2_out, not_2_out, lights_1_s1, lights_1_s0);
  not not_3 (not_3_out, undriven);
  Multiplexer #(.enable("false")) multiplexer_1 (.in0(1'b1), .in1(undriven), .out(multiplexer_1_out), .sel(and_2_out));
  D_Flip_Flop d_ff_1 (
    .D(multiplexer_1_out), .clk(multiplexer_2_out), .Q(d_ff_1_q), .Qn(d_ff_1_qn));  // open: preset, reset
  Multiplexer #(.enable("false")) multiplexer_2 (
    .in0(undriven), .in1(not_3_out), .out(multiplexer_2_out), .sel(and_2_out));
  Hex_Digit_Display hex_digit_display_1 (.value({3'b000, delay_1_delay[4]}));  // open: dp
  Hex_Digit_Display hex_digit_display_2 (.value(delay_1_delay[3:0]));  // open: dp
  not not_4 (not_4_out, lights_1_s0);
  or or_2 (or_2_out, d_ff_1_qn, delay_1_twenty_five);
  and and_3 (and_3_out, d_ff_1_q, not_4_out, delay_1_twenty_five);
  and and_4 (and_4_out, and_2_out, or_2_out);
  or or_3 (or_3_out, and_4_out, and_3_out, delay_1_four, delay_1_two);
  LED led_1 (.in(lights_1_y1));
  LED led_2 (.in(lights_1_y2));
  LED led_3 (.in(lights_1_y3));
  lights lights_1 (
    .clk(or_3_out), .Y1(lights_1_y1), .Y2(lights_1_y2), .Y3(lights_1_y3), .Y4(lights_1_y4), .Y5(lights_1_y5),
    .Y6(lights_1_y6), .S2(lights_1_s2), .S1(lights_1_s1), .S0(lights_1_s0));
  LED led_4 (.in(lights_1_y4));
  LED led_5 (.in(lights_1_y5));
  LED led_6 (.in(lights_1_y6));

  // Notes on the sheet:
  //   Delay
  //   Lights
endmodule

module lights (
  input  clk,
  output Y1,
  output Y2,
  output Y3,
  output Y4,
  output Y5,
  output Y6,
  output S2,
  output S1,
  output S0
);

  wire and_1_out, and_2_out, not_1_out, not_2_out, not_3_out;

  Counter #(.width(3), .max('h5)) counter_1 (.clk(clk), .Q({S2, S1, S0}));  // open: clr, load, up, count, D, carry
  not not_1 (not_1_out, S1);
  not not_2 (not_2_out, S0);
  not not_3 (not_3_out, S2);
  and and_1 (and_1_out, not_1_out, S0);
  and and_2 (and_2_out, not_2_out, not_3_out);
  and and_3 (Y5, S2, not_1_out, not_2_out);
  and and_4 (Y6, not_3_out, S1, S0);
  xor xor_1 (Y1, S2, S1);
  and and_5 (Y2, not_3_out, not_1_out, S0);
  and and_6 (Y3, not_3_out, not_1_out, not_2_out);
  or or_1 (Y4, and_1_out, and_2_out);
  LED led_1 (.in(Y1));
  LED led_2 (.in(Y2));
  LED led_3 (.in(Y3));
  LED led_4 (.in(Y4));
  LED led_5 (.in(Y5));
  LED led_6 (.in(Y6));
endmodule

module delay (
  input  S2,
  input  S1,
  input  S0,
  input  clk,
  output Twenty_five,
  output Four,
  output [4:0] Delay,
  output Two
);

  wire and_1_out, and_2_out, and_3_out, nand_1_out, nand_2_out, nand_3_out, nand_4_out, nand_5_out,
       nand_6_out, not_1_out, not_2_out, not_3_out;
  wire [1:0] counter_3_q;
  wire [2:0] counter_1_q, counter_2_q;

  not not_1 (not_1_out, S2);
  not not_2 (not_2_out, S1);
  not not_3 (not_3_out, S0);
  nand nand_1 (nand_1_out, not_3_out, not_2_out, not_1_out);
  nand nand_2 (nand_2_out, not_1_out, S1, S0);
  nand nand_3 (nand_3_out, not_1_out, not_2_out, S0);
  nand nand_4 (nand_4_out, S2, not_2_out, not_3_out);
  nand nand_5 (nand_5_out, not_1_out, S1, not_3_out);
  nand nand_6 (nand_6_out, S2, not_2_out, S0);
  and and_1 (and_1_out, nand_1_out, nand_2_out);
  and and_2 (and_2_out, nand_3_out, nand_4_out);
  and and_3 (and_3_out, nand_5_out, nand_6_out);
  Counter #(.width(5), .max('h19), .ongoal("stay")) counter_1 (
    .clr(and_1_out), .clk(clk), .carry(Twenty_five), .Q({Delay[4:3], counter_1_q}));  // open: load, up, count, D
  Counter #(.width(3), .max('h4), .ongoal("stay")) counter_2 (
    .clr(and_2_out), .clk(clk), .carry(Four), .Q(counter_2_q));  // open: load, up, count, D
  Counter #(.width(2), .max('h2), .ongoal("stay")) counter_3 (
    .clr(and_3_out), .clk(clk), .carry(Two), .Q(counter_3_q));  // open: load, up, count, D
  or or_1 (Delay[2], counter_1_q[2], counter_2_q[2]);
  or or_2 (Delay[1], counter_1_q[1], counter_2_q[1], counter_3_q[1]);
  or or_3 (Delay[0], counter_1_q[0], counter_2_q[0], counter_3_q[0]);
endmodule
