// Logisim project Booths_multiplier.circ as structural Verilog: 3 circuits, main circuit main
module main (
  input  [15:0] B,
  input  [15:0] Q,
  input  Load,
  input  LE,
  output [31:0] Result
);

  wire clock_1_out, controlled_buffer_1_out, counter_1_carry, not_1_out, or_1_out;
  wire [0:0] register_1_q;
  wire [15:0] alu_1_out_4, Multiplicand_q;
  wire [32:0] multiplexer_1_out, shifter_1_out;

  Clock clock_1 (.out(clock_1_out));
  Multiplexer #(.width(33)) multiplexer_1 (
    .in0(shifter_1_out), .in1({{16{1'b0}}, Q, 1'b0}), .out(multiplexer_1_out), .sel(LE));
  assign controlled_buffer_1_out = not_1_out ? clock_1_out : 1'bz;  // Controlled_Buffer controlled_buffer_1
  Register #(.width(16)) Multiplicand (.D(B), .clk(Load), .Q(Multiplicand_q));  // open: en, clr
  Register #(.width(33)) register_1 (
    .D(multiplexer_1_out), .clk(or_1_out), .Q({Result, register_1_q[0]}));  // open: en, clr
  or or_1 (or_1_out, Load, controlled_buffer_1_out);
  Counter #(.max('h10), .width(5)) counter_1 (
    .clk(controlled_buffer_1_out), .carry(counter_1_carry));  // open: clr, load, up, count, D, Q
  not not_1 (not_1_out, counter_1_carry);
  ALU alu_1 (.A(Result[31:16]), .B(Multiplicand_q), .S({Result[0], register_1_q[0]}), .out_4(alu_1_out_4));
  Shifter #(.shift("ar"), .width(33)) shifter_1 (
    .in({alu_1_out_4, Result[15:0], register_1_q[0]}), .\dist (6'b000001), .out(shifter_1_out));
endmodule

module ALU (
  input  [15:0] A,
  input  [15:0] B,
  input  [1:0] S,
  output [15:0] out_4
);

  wire [15:0] multiplexer_1_out, not_1_out;

  assign not_1_out = ~B;  // NOT_Gate not_1, 16 bits wide
  Multiplexer #(.select(2), .width(16)) multiplexer_1 (
    .in0({16{1'b0}}), .in1(B), .in2(not_1_out), .in3({16{1'b0}}), .out(multiplexer_1_out), .sel(S));
  Adder #(.width(16)) adder_1 (.a(A), .b(multiplexer_1_out), .out(out_4), .cin(S[1]));  // open: cout
endmodule

module bm_old (
  input  [15:0] B,
  input  [15:0] O,
  input  Load
);

  wire clock_1_out, controlled_buffer_1_out, controlled_buffer_2_out, counter_1_carry, not_1_out, or_1_out,
       t_ff_1_qn;
  wire [15:0] alu_1_out_4, multiplexer_1_out, multiplexer_2_out, Multiplicand_q, Q_q;
  wire [32:0] d_ff_1_q, shifter_1_out;

  Clock clock_1 (.out(clock_1_out));
  assign controlled_buffer_1_out = not_1_out ? clock_1_out : 1'bz;  // Controlled_Buffer controlled_buffer_1
  Counter #(.max('h20), .width(6)) counter_1 (
    .clk(controlled_buffer_1_out), .carry(counter_1_carry));  // open: clr, load, up, count, D, Q
  Register #(.width(16)) Multiplicand (.D(B), .clk(Load), .Q(Multiplicand_q));  // open: en, clr
  Multiplexer #(.width(16)) multiplexer_1 (
    .in0(alu_1_out_4), .in1(shifter_1_out[32:17]), .out(multiplexer_1_out), .sel(t_ff_1_qn));
  T_Flip_Flop t_ff_1 (.T(1'b1), .clk(controlled_buffer_1_out), .Qn(t_ff_1_qn));  // open: Q, reset, preset
  Register #(.trigger("falling"), .width(16)) A (
    .D(multiplexer_1_out), .clk(controlled_buffer_1_out), .Q(d_ff_1_q[32:17]));  // open: en, clr
  not not_1 (not_1_out, counter_1_carry);
  Multiplexer #(.width(16)) multiplexer_2 (.in0(shifter_1_out[16:1]), .in1(O), .out(multiplexer_2_out), .sel(Load));
  Register #(.trigger("falling"), .width(16)) Q (
    .D(multiplexer_2_out), .en(t_ff_1_qn), .clk(or_1_out), .Q(Q_q));  // open: clr
  or or_1 (or_1_out, Load, controlled_buffer_1_out);
  ALU alu_1 (.A(d_ff_1_q[32:17]), .B(Multiplicand_q), .S({Q_q[0], d_ff_1_q[0]}), .out_4(alu_1_out_4));
  D_Flip_Flop #(.trigger("falling")) d_ff_1 (
    .D(controlled_buffer_2_out), .clk(controlled_buffer_1_out), .Q(d_ff_1_q[0]));  // open: Qn, preset, reset
  assign controlled_buffer_2_out = t_ff_1_qn ? shifter_1_out[0] : 1'bz;  // Controlled_Buffer controlled_buffer_2
  Shifter #(.shift("ar"), .width(33)) shifter_1 (
    .in({d_ff_1_q[32:17], Q_q, d_ff_1_q[0]}), .\dist (6'b000001), .out(shifter_1_out));
endmodule
