// Logisim project Hardwired_control_unit.circ as structural Verilog: 3 circuits, main circuit main
module main (
  input  [15:0] in_1,
  input  Load_PC,
  output [15:0] out_3,
  output [15:0] out_4,
  output [15:0] out_5,
  output [15:0] out_6,
  output [15:0] out_7,
  output [15:0] out_8
);

  wire Clk_out, decoder_2_out1;
  wire [1:1] decoder_2_out0;
  wire [3:0] counter_1_q;
  wire [15:0] alu_1_o, multiplexer_1_out, ram_1_dout;

  ALU alu_1 (.A(out_7), .B(out_6), .O(alu_1_o));  // open: cin_bin, Sub, cout_bout
  Multiplexer #(.width(16)) multiplexer_1 (.in0(out_3), .in1(in_1), .out(multiplexer_1_out), .sel(Load_PC));
  RAM #(.addrWidth(12), .dataWidth(16), .trigger("high")) ram_1 (
    .addr(out_4[11:0]), .dout(ram_1_dout));  // open: we, oe, din
  modified_reg AR (.I(out_3), .L(decoder_2_out0[1]), .O(out_4));  // open: Inc, Clr
  modified_reg PC (.I(multiplexer_1_out), .L(Load_PC), .Inc(decoder_2_out1), .O(out_5));  // open: Clr
  modified_reg DR (.I(out_3), .O(out_6));  // open: L, Inc, Clr
  modified_reg AC (.I(alu_1_o), .O(out_7));  // open: L, Inc, Clr
  modified_reg IR (.I(out_3), .L(decoder_2_out1), .O(out_8));  // open: Inc, Clr
  Clock Clk (.out(Clk_out));
  D_Flip_Flop I (.D(out_8[15]), .clk(Clk_out));  // open: Q, Qn, preset, reset
  Decoder #(.select(3)) decoder_1 (.sel(out_8[14:12]));  // open: out0, out1, out2, out3, out4, out5, out6, out7, en
  Multiplexer #(.select(3), .width(16)) multiplexer_2 (
    .in0(ram_1_dout), .in1(out_4), .in2(out_5), .in3(out_6), .in4(out_7), .in5({4'b0000, out_8[11:0]}),
    .out(out_3), .sel({1'b0, decoder_2_out0[1], 1'b0}));  // open: in6, in7
  Counter #(.max('hf), .width(4)) counter_1 (.clk(Clk_out), .Q(counter_1_q));  // open: clr, load, up, count, D, carry
  Decoder #(.select(4)) decoder_2 (
    .out0(decoder_2_out0[1]), .out1(decoder_2_out1), .sel(counter_1_q));  // open: out2, out3, out4, out5, out6, out7, out8, out9, out10, out11, out12, out13, out14, out15, en
endmodule

module modified_reg (
  input  [15:0] I,
  input  L,
  input  Inc,
  input  Clr,
  output [15:0] O
);

  wire or_1_out;
  wire [15:0] adder_1_out, multiplexer_1_out;

  Register #(.trigger("falling"), .width(16)) register_1 (
    .D(multiplexer_1_out), .clk(or_1_out), .Q(O), .clr(Clr));  // open: en
  Multiplexer #(.width(16)) multiplexer_1 (.in0(I), .in1(adder_1_out), .out(multiplexer_1_out), .sel(Inc));
  or or_1 (or_1_out, L, Inc);
  Adder #(.width(16)) adder_1 (.a(O), .b({16{1'b0}}), .out(adder_1_out), .cin(1'b1));  // open: cout
endmodule

module ALU (
  input  cin_bin,
  input  [15:0] A,
  input  [15:0] B,
  input  Sub,
  output cout_bout,
  output [15:0] O
);

  wire adder_1_cout, subtractor_1_bout;
  wire [15:0] adder_1_out, subtractor_1_out;

  Adder #(.width(16)) adder_1 (.a(A), .b(B), .out(adder_1_out), .cin(cin_bin), .cout(adder_1_cout));
  Subtractor #(.width(16)) subtractor_1 (.a(A), .b(B), .out(subtractor_1_out), .bin(cin_bin), .bout(subtractor_1_bout));
  Multiplexer #(.width(16)) multiplexer_1 (.in0(adder_1_out), .in1(subtractor_1_out), .out(O), .sel(Sub));
  Multiplexer multiplexer_2 (.in0(adder_1_cout), .in1(subtractor_1_bout), .out(cout_bout), .sel(Sub));
endmodule
