// Logisim project Register_file_and_alu.circ as structural Verilog: 3 circuits, main circuit main
module main (
  input  [7:0] in_1,
  input  in_2,
  input  [1:0] Sel_w,
  input  [1:0] Sel_r1,
  input  [1:0] Sel_r0,
  input  Choose_op,
  output [7:0] out_7,
  output [7:0] out_8,
  output C
);

  wire clock_1_out;
  wire [7:0] alu_1_out_5, multiplexer_1_out;

  Clock clock_1 (.out(clock_1_out));
  Multiplexer #(.width(8), .enable("false")) multiplexer_1 (
    .in0(in_1), .in1(alu_1_out_5), .out(multiplexer_1_out), .sel(in_2));
  Register_file register_file_1 (
    .Din(multiplexer_1_out), .Select_w(Sel_w), .Select_reg0(Sel_r0), .Clk(clock_1_out), .S0(out_7),
    .S1(out_8), .Select_reg1(Sel_r1));
  ALU alu_1 (.Op1(out_7), .Op2(out_8), .out_5(alu_1_out_5), .Select_op(Choose_op), .Flag(C));
endmodule

module ALU (
  input  [7:0] Op1,
  input  [7:0] Op2,
  input  Select_op,
  output Flag,
  output [7:0] out_5
);

  wire adder_1_cout, subtractor_1_bout;
  wire [7:0] adder_1_out, subtractor_1_out;

  Adder adder_1 (.a(Op1), .b(Op2), .out(adder_1_out), .cout(adder_1_cout));  // open: cin
  Subtractor subtractor_1 (.a(Op1), .b(Op2), .out(subtractor_1_out), .bout(subtractor_1_bout));  // open: bin
  Multiplexer #(.enable("false")) multiplexer_1 (
    .in0(adder_1_cout), .in1(subtractor_1_bout), .out(Flag), .sel(Select_op));
  Multiplexer #(.width(8), .enable("false")) multiplexer_2 (
    .in0(adder_1_out), .in1(subtractor_1_out), .out(out_5), .sel(Select_op));
endmodule

module Register_file (
  input  [7:0] Din,
  input  [1:0] Select_w,
  input  [1:0] Select_reg1,
  input  [1:0] Select_reg0,
  input  Clk,
  output [7:0] S0,
  output [7:0] S1
);

  wire decoder_1_out0, decoder_1_out1, decoder_1_out2, decoder_1_out3;
  wire [7:0] register_1_q, register_2_q, register_3_q, register_4_q;

  Decoder #(.select(2)) decoder_1 (
    .out0(decoder_1_out0), .out1(decoder_1_out1), .out2(decoder_1_out2), .out3(decoder_1_out3), .sel(Select_w));  // open: en
  Register register_1 (.D(Din), .en(decoder_1_out0), .clk(Clk), .Q(register_1_q));  // open: clr
  Register register_2 (.D(Din), .en(decoder_1_out1), .clk(Clk), .Q(register_2_q));  // open: clr
  Register register_3 (.D(Din), .en(decoder_1_out2), .clk(Clk), .Q(register_3_q));  // open: clr
  Register register_4 (.D(Din), .en(decoder_1_out3), .clk(Clk), .Q(register_4_q));  // open: clr
  Multiplexer #(.select(2), .width(8), .enable("false")) multiplexer_1 (
    .in0(register_1_q), .in1(register_2_q), .in2(register_3_q), .in3(register_4_q), .out(S1),
    .sel(Select_reg1));
  Multiplexer #(.select(2), .width(8), .enable("false")) multiplexer_2 (
    .in0(register_1_q), .in1(register_2_q), .in2(register_3_q), .in3(register_4_q), .out(S0),
    .sel(Select_reg0));
endmodule
