// Logisim project alu_complete.circ as structural Verilog
module ALU (
  input  [3:0] A,
  input  [3:0] B,
  input  [2:0] Sel1,
  input  [1:0] Sel2,
  output [3:0] O
);

  wire [3:0] adder_1_out, and_1_out, and_2_out, multiplexer_1_out, multiplexer_2_out, not_1_out, not_2_out,
       not_3_out, or_1_out, shifter_1_out, shifter_2_out, xor_1_out;

  assign and_1_out = A & B;  // AND_Gate and_1, 4 bits wide
  assign or_1_out = A | B;  // OR_Gate or_1, 4 bits wide
  assign xor_1_out = A ^ B;  // XOR_Gate xor_1, 4 bits wide
  assign not_1_out = ~A;  // NOT_Gate not_1, 4 bits wide
  assign and_2_out = A & not_2_out;  // AND_Gate and_2, 4 bits wide
  assign not_2_out = ~B;  // NOT_Gate not_2, 4 bits wide
  assign not_3_out = ~B;  // NOT_Gate not_3, 4 bits wide
  Multiplexer #(.select(2), .width(4)) multiplexer_1 (
    .in0(B), .in1(not_3_out), .in2(4'b0000), .in3(4'b1111), .out(multiplexer_1_out), .sel(Sel1[1:0]));
  Adder #(.width(4)) adder_1 (.a(A), .b(multiplexer_1_out), .out(adder_1_out), .cin(Sel1[2]));  // open: cout
  Multiplexer #(.select(3), .width(4)) multiplexer_2 (
    .in0(and_1_out), .in1(or_1_out), .in2(xor_1_out), .in3(not_1_out), .in4(or_1_out), .in5(and_2_out),
    .in6(xor_1_out), .in7(or_1_out), .out(multiplexer_2_out), .sel(Sel1));
  Shifter #(.width(4)) shifter_1 (.in(A), .\dist (2'b01), .out(shifter_1_out));
  Shifter #(.shift("ar"), .width(4)) shifter_2 (.in(A), .\dist (2'b01), .out(shifter_2_out));
  Multiplexer #(.select(2), .width(4)) multiplexer_3 (
    .in0(adder_1_out), .in1(multiplexer_2_out), .in2(shifter_1_out), .in3(shifter_2_out), .out(O), .sel(Sel2));
endmodule
