// Logisim project ip_class_netid_hostid.circ as structural Verilog: 1 circuit, main circuit main
module main (
  input  [7:0] in_1,
  input  [7:0] in_2,
  input  [7:0] in_3,
  input  [7:0] in_4,
  input  [7:0] in_5,
  input  [7:0] in_6,
  output [7:0] out_7,
  output [7:0] out_8,
  output [7:0] out_9,
  output [7:0] out_10,
  output [7:0] out_11,
  output [7:0] out_12,
  output [7:0] out_13,
  output [7:0] out_14
);

  wire and_1_out, and_2_out, and_3_out, and_4_out, clock_1_out, not_1_out, not_2_out, not_3_out, not_4_out,
       or_1_out, or_2_out;
  wire [7:0] multiplexer_1_out, multiplexer_2_out, multiplexer_3_out;
  wire [31:0] IP_addr_q, not_5_out;

  Multiplexer #(.width(8)) multiplexer_1 (.in0(in_1), .in1(in_2), .out(multiplexer_1_out), .sel(or_1_out));
  Clock clock_1 (.out(clock_1_out));
  Register #(.width(32)) IP_addr (.D({in_6, in_5, in_4, in_3}), .clk(clock_1_out), .Q(IP_addr_q));  // open: en, clr
  Multiplexer #(.width(8)) multiplexer_2 (.in0(in_1), .in1(in_2), .out(multiplexer_2_out), .sel(or_2_out));
  Multiplexer #(.width(8)) multiplexer_3 (.in0(in_1), .in1(in_2), .out(multiplexer_3_out), .sel(and_3_out));
  not not_1 (not_1_out, IP_addr_q[31]);
  not not_2 (not_2_out, IP_addr_q[30]);
  not not_3 (not_3_out, IP_addr_q[28]);
  not not_4 (not_4_out, IP_addr_q[28]);
  and and_1 (and_1_out, IP_addr_q[31], not_2_out);
  and and_2 (and_2_out, IP_addr_q[31], IP_addr_q[30], not_3_out);
  and and_3 (and_3_out, IP_addr_q[31], IP_addr_q[30], IP_addr_q[29], not_4_out);
  and and_4 (and_4_out, IP_addr_q[31], IP_addr_q[30], IP_addr_q[29], IP_addr_q[28]);
  assign not_5_out = ~{multiplexer_1_out, multiplexer_2_out, multiplexer_3_out, in_1};  // NOT_Gate not_5, 32 bits wide
  or or_1 (or_1_out, not_1_out, and_1_out, and_2_out);
  or or_2 (or_2_out, and_1_out, and_2_out);
  LED A (.in(not_1_out));
  LED B (.in(and_1_out));
  LED C (.in(and_2_out));
  LED D (.in(and_3_out));
  LED E (.in(and_4_out));
  assign {out_10, out_9, out_8, out_7} = {multiplexer_1_out, multiplexer_2_out, multiplexer_3_out, in_1} & IP_addr_q;  // AND_Gate and_5, 32 bits wide
  assign {out_14, out_13, out_12, out_11} = not_5_out & IP_addr_q;  // AND_Gate and_6, 32 bits wide

  // Notes on the sheet:
  //   in_2: initial=0xff
  //   in_3: initial=0x58
  //   in_4: initial=0x1d
  //   in_5: initial=0xa8
  //   in_6: initial=0xc0
  //   NetID
  //   HostID
endmodule
